// Logisim project imm_gen.circ as structural Verilog: 1 circuit, main circuit imm_gen
module imm_gen (
  input  [31:0] inst,
  input  [2:0] ImmSel,
  output [31:0] imm
);

  wire [31:0] B_imm, I_imm, J_imm, S_imm;

  assign I_imm = {{20{inst[31]}}, inst[31:20]};  // Bit_Extender bit_extender_1
  assign S_imm = {{20{inst[31]}}, {inst[31:25], inst[11:7]}};  // Bit_Extender bit_extender_2
  assign B_imm = {{19{inst[31]}}, {inst[31], inst[7], inst[30:25], inst[11:8], 1'b0}};  // Bit_Extender bit_extender_3
  assign J_imm = {{11{inst[31]}}, {inst[31], inst[19:12], inst[20], inst[30:21], 1'b0}};  // Bit_Extender bit_extender_4
  // Probe on imm
  Multiplexer #(.select(3), .width(32), .enable("false")) multiplexer_1 (
    .in0({32{1'b0}}), .in1(I_imm), .in2(S_imm), .in3(B_imm), .in4({inst[31:12], {12{1'b0}}}), .in5(J_imm),
    .in6({32{1'b0}}), .in7({32{1'b0}}), .out(imm), .sel(ImmSel));
  // Probe on I_imm
  // Probe on S_imm
  // Probe on B_imm
  // Probe on {inst[31:12], {12{1'b0}}}
  // Probe on J_imm

  // Other names for the same wires on the sheet: U_imm[31:12] = inst[31:12]; funct3[2:0] = inst[14:12];
  //   opcode[6:0] = inst[6:0]

  // Notes on the sheet:
  //   INPUTS to your circuit
  //   DON'T CHANGE THE LOCATIONS OF THE INPUTS AND OUTPUTS!
  //   OUTPUT from your circuit
endmodule
